# Fritzing sketch Shield Progra (saved by Fritzing 0.9.0b)
circuit board: 7.42351cm x 5.4081cm
breadboards: 1

parts:
  U1 = atmega328 [package=dip]
  U2 = ATmega644 [package=pdpi]
  U3 = attiny85 [package=dip]
  Attiny_2313 = IC, DIP package, 20 pins [chip_label=IC]
  HeartBeat = LED - 5mm [color="Yellow (595nm)" package="5 mm [THT]"]
  Progrsso = LED - 5mm [color="Green (570nm)" package="5 mm [THT]"]
  Error = LED - 5mm [color="Red (633nm)" package="5 mm [THT]"]
  LED1 = LED - 5mm [color="Red (633nm)" package="5 mm [THT]"]
  R1 = Resistor [tolerance=±5% resistance=120 package=THT]
  R3 = Resistor [tolerance=±5% resistance=120 package=THT]
  C1 = Electrolytic Capacitor [capacitance=1µF package="100 mil [THT, electrolytic]"]
  XTAL1 = Crystal [frequency="16 Mhz" package=THT]
  C3 = Ceramic Capacitor [capacitance=100nF package="100 mil [THT, multilayer]"]
  C2 = Ceramic Capacitor [capacitance=100nF package="100 mil [THT, multilayer]"]
  Attiny84/44 = IC, DIP package, 14 pins [chip_label=IC]
  Componente1 = Arduino Uno (Rev3)

nets:
  N1: U1.RESET, U2.RESET, U3.Pin_1, Attiny_2313.pin1, Attiny84/44.pin4, Componente1.D10_PWM/SS
  5V: U1.VCC, U1.AVCC, U2.VCC, U3.Pin_8, Attiny_2313.pin20, Attiny84/44.pin1, Componente1.5V
  GND: U1.GND, U2.GND, U3.Pin_4, Attiny_2313.pin10, R1.Pin_0, R3.Pin_0, C1.-, C3.0, C2.0, Attiny84/44.pin14, Componente1.GND
  N2: U1.XLAT1, XTAL1.pin_1, C3.1
  N3: U1.XLAT2, XTAL1.pin_0, C2.1
  N4: U1.D9_(PWM), U2.PD5, Attiny_2313.pin16, LED1.anode
  N5: U1.D11_(PWM), U2.PB5, U3.Pin_5, Attiny_2313.pin17, Attiny84/44.pin7, Componente1.D11_PWM/MOSI
  N6: U1.D12, U2.PB6, U3.Pin_6, Attiny_2313.pin18, Attiny84/44.pin8, Componente1.D12/MISO
  N7: U1.D13, U2.PB7, U3.Pin_7, Attiny_2313.pin19, Attiny84/44.pin9, Componente1.D13/SCK
  N8: HeartBeat.cathode, Progrsso.cathode, Error.cathode, R1.Pin_1
  N9: HeartBeat.anode, Componente1.D9_PWM
  N10: Progrsso.anode, Componente1.D7
  N11: Error.anode, Componente1.D8
  N12: LED1.cathode, R3.Pin_1
  N13: C1.+, Componente1.RESET

notes:
  Atmega 328/8/32/16
